// Logisim project ALU.circ as structural Verilog
module ALU (
  input  [7:0] X,
  input  [7:0] Y,
  input  [3:0] in_3,
  output [7:0] Z,
  output O
);

  wire sabirac_1_of, subtractor_1_of;
  wire [7:0] and_1_out, not_1_out, or_1_out, rol_1_out_3, ror_1_out_3, sabirac_1_rezultat, shl_1_out_3,
       shr_1_out_3, subtractor_1_z;

  Sabirac sabirac_1 (.X(X), .Y(Y), .Rezultat(sabirac_1_rezultat), .OF(sabirac_1_of));
  Subtractor subtractor_1 (.X(X), .Y(Y), .Z(subtractor_1_z), .OF(subtractor_1_of));
  SHL shl_1 (.in_1(X), .X(Y), .out_3(shl_1_out_3));
  SHR shr_1 (.in_1(X), .X(Y), .out_3(shr_1_out_3));
  ROL rol_1 (.in_1(X), .X(Y), .out_3(rol_1_out_3));
  ROR ror_1 (.in_1(X), .X(Y), .out_3(ror_1_out_3));
  assign not_1_out = ~X;  // NOT_Gate not_1, 8 bits wide
  assign and_1_out = X & Y;  // AND_Gate and_1, 8 bits wide
  assign or_1_out = Y | X;  // OR_Gate or_1, 8 bits wide
  Multiplexer #(.select(4), .width(8)) multiplexer_1 (
    .in0(X), .in1(X), .in2(X), .in3(sabirac_1_rezultat), .in4(subtractor_1_z), .in5({8{1'b0}}), .in6(X),
    .in7(shl_1_out_3), .in8(shr_1_out_3), .in9(rol_1_out_3), .in10(ror_1_out_3), .in11(not_1_out),
    .in12(and_1_out), .in13(or_1_out), .in14({8{1'b1}}), .in15({8{1'b1}}), .out(Z), .sel(in_3));  // open: en
  or or_2 (O, sabirac_1_of, subtractor_1_of);
endmodule
